// Logisim project ALU.circ as structural Verilog: 5 circuits, main circuit ALU
module ALU (
  input  [31:0] in_1,
  input  [31:0] in_2,
  input  [3:0] Operation,
  output [31:0] out_4,
  output [31:0] out_5
);

  wire slt_bit, sltu_bit;
  wire [31:0] Add, AND, DivHigh, DivLow, DivuHigh, DivuLow, MultHigh, MultLow, MuluHigh, MuluLow, NOR, OR,
       Slt, Sltu, Sub, XOR;

  Adder #(.width(32)) adder_1 (.a(in_1), .b(in_2), .out(Add));  // open: cin, cout
  Multiplier #(.width(32)) multiplier_1 (.a(in_1), .b(in_2), .out(MuluLow), .cout(MuluHigh));  // open: cin
  Comparator #(.width(32)) comparator_1 (.a(in_1), .b(in_2), .lt(slt_bit));  // open: gt, eq
  assign Slt = {{31{1'b0}}, slt_bit};  // Bit_Extender bit_extender_1
  Multiplicar multiplicar_1 (.in_1(in_1), .in_2(in_2), .out_3(MultLow), .out_4(MultHigh));
  Comparator #(.width(32), .mode("unsigned")) comparator_2 (.a(in_1), .b(in_2), .lt(sltu_bit));  // open: gt, eq
  assign Sltu = {{31{1'b0}}, sltu_bit};  // Bit_Extender bit_extender_2
  Subtractor #(.width(32)) subtractor_1 (.a(in_1), .b(in_2), .out(Sub));  // open: bin, bout
  Divider #(.width(32)) divider_1 (.a(in_1), .b(in_2), .out(DivuLow), .rem(DivuHigh));  // open: upper
  Dividir dividir_1 (.in_1(in_1), .in_2(in_2), .out_3(DivLow), .out_4(DivHigh));
  Multiplexer #(.select(2), .width(32), .enable("false")) multiplexer_1 (
    .in0(MultHigh), .in1(MuluHigh), .in2(DivHigh), .in3(DivuHigh), .out(out_4), .sel(Operation[1:0]));
  assign AND = in_1 & in_2;  // AND_Gate and_1, 32 bits wide
  assign OR = in_1 | in_2;  // OR_Gate or_1, 32 bits wide
  Multiplexer #(.select(4), .width(32), .enable("false")) multiplexer_2 (
    .in0(Add), .in1(Sub), .in2(Slt), .in3(Sltu), .in4(AND), .in5(OR), .in6(NOR), .in7(XOR), .in8(MultLow),
    .in9(MuluLow), .in10(DivLow), .in11(DivuLow), .out(out_5), .sel(Operation));  // open: in12, in13, in14, in15
  assign XOR = in_1 ^ in_2;  // XOR_Gate xor_1, 32 bits wide
  assign NOR = ~(in_1 | in_2);  // NOR_Gate nor_1, 32 bits wide

  // Other names for the same wires on the sheet: A[31:0] = in_1; ALU_Output[31:0] = out_5; B[31:0] = in_2;
  //   High[31:0] = out_4; HighSelector[1:0] = Operation[1:0]; Selector[3:0] = Operation

  // Notes on the sheet:
  //   Inputs
  //   Data
  //   Arithmetic
  //   Logic
  //   High output
  //   Alu output
endmodule

module Negative_To_Positive (
  input  [31:0] in_1,
  output [31:0] out_2,
  output Carry_Output
);

  wire [31:0] not_1_out;

  assign not_1_out = ~in_1;  // NOT_Gate not_1, 32 bits wide
  Adder #(.width(32)) adder_1 (.a(not_1_out), .b(32'h1), .out(out_2), .cout(Carry_Output));  // open: cin

  // Notes on the sheet:
  //   Input
  //   Positive Output
endmodule

module ABS (
  input  [31:0] in_1,
  output [31:0] out_2,
  output out_3
);

  wire [31:0] negative_to_positive_1_out_2;

  Negative_To_Positive negative_to_positive_1 (
    .in_1(in_1), .out_2(negative_to_positive_1_out_2));  // open: Carry_Output
  Multiplexer #(.width(32), .enable("false")) multiplexer_1 (
    .in0(in_1), .in1(negative_to_positive_1_out_2), .out(out_2), .sel(in_1[31]));

  assign out_3 = in_1[31];
endmodule

module Multiplicar (
  input  [31:0] in_1,
  input  [31:0] in_2,
  output [31:0] out_3,
  output [31:0] out_4
);

  wire isNeg, negative_to_positive_1_carry_output, signA, signB;
  wire [31:0] abs_1_out_2, abs_2_out_2, adder_1_out, multiplier_1_cout, multiplier_1_out,
       negative_to_positive_1_out_2, not_1_out;

  ABS abs_1 (.in_1(in_1), .out_2(abs_1_out_2), .out_3(signA));
  ABS abs_2 (.in_1(in_2), .out_2(abs_2_out_2), .out_3(signB));
  xor xor_1 (isNeg, signA, signB);
  Multiplier #(.width(32)) multiplier_1 (
    .a(abs_1_out_2), .b(abs_2_out_2), .out(multiplier_1_out), .cout(multiplier_1_cout));  // open: cin
  assign not_1_out = ~multiplier_1_cout;  // NOT_Gate not_1, 32 bits wide
  Negative_To_Positive negative_to_positive_1 (
    .in_1(multiplier_1_out), .out_2(negative_to_positive_1_out_2),
    .Carry_Output(negative_to_positive_1_carry_output));
  Adder #(.width(32)) adder_1 (
    .a(not_1_out), .b({32{1'b0}}), .out(adder_1_out), .cin(negative_to_positive_1_carry_output));  // open: cout
  Multiplexer #(.width(32), .enable("false")) multiplexer_1 (
    .in0(multiplier_1_out), .in1(negative_to_positive_1_out_2), .out(out_3), .sel(isNeg));
  Multiplexer #(.width(32), .enable("false")) multiplexer_2 (
    .in0(multiplier_1_cout), .in1(adder_1_out), .out(out_4), .sel(isNeg));

  // Notes on the sheet:
  //   A
  //   B
  //   Low
  //   High
endmodule

module Dividir (
  input  [31:0] in_1,
  input  [31:0] in_2,
  output [31:0] out_3,
  output [31:0] out_4
);

  wire isNeg, signA, signB;
  wire [31:0] abs_1_out_2, abs_2_out_2, divider_1_out, divider_1_rem, negative_to_positive_1_out_2,
       negative_to_positive_2_out_2;

  ABS abs_1 (.in_1(in_1), .out_2(abs_1_out_2), .out_3(signA));
  ABS abs_2 (.in_1(in_2), .out_2(abs_2_out_2), .out_3(signB));
  xor xor_1 (isNeg, signA, signB);
  Divider #(.width(32)) divider_1 (
    .a(abs_1_out_2), .b(abs_2_out_2), .out(divider_1_out), .rem(divider_1_rem));  // open: upper
  Negative_To_Positive negative_to_positive_1 (
    .in_1(divider_1_out), .out_2(negative_to_positive_1_out_2));  // open: Carry_Output
  Negative_To_Positive negative_to_positive_2 (
    .in_1(divider_1_rem), .out_2(negative_to_positive_2_out_2));  // open: Carry_Output
  Multiplexer #(.width(32), .enable("false")) multiplexer_1 (
    .in0(divider_1_out), .in1(negative_to_positive_1_out_2), .out(out_3), .sel(isNeg));
  Multiplexer #(.width(32), .enable("false")) multiplexer_2 (
    .in0(divider_1_rem), .in1(negative_to_positive_2_out_2), .out(out_4), .sel(isNeg));

  // Notes on the sheet:
  //   Low
  //   High
endmodule
