// Logisim project Control Unit.circ as structural Verilog: 10 circuits, main circuit Control Unit
module Control_Unit (
  input  [5:0] in_1,
  input  in_2,
  input  in_3,
  input  [5:0] in_4,
  input  in_5,
  input  in_6,
  output out_7,
  output [2:0] out_8,
  output out_9,
  output out_10,
  output out_11,
  output out_12,
  output out_13,
  output out_14,
  output out_15,
  output out_16,
  output out_17,
  output [2:0] out_18,
  output out_19,
  output out_20,
  output out_21,
  output [3:0] out_22,
  output out_23,
  output [1:0] out_24,
  output [2:0] out_25
);

  wire _mem, _pc, _RF, demultiplexer_2_out0, demultiplexer_2_out1, demultiplexer_3_out0,
       demultiplexer_3_out1, demultiplexer_5_out0, demultiplexer_6_out3, End_q, end_read, end_write, Fetch_q,
       get_data_1, get_data_2, halt, Idle_q, is_hi_lo, Is_Inst, Is_Jump, is_PC, is_RF, kbd, Mem, Mem_Read,
       Mem_Write, multiplexer_1_out, not_1_out, or_1_out, or_3_out, Save_2_q, Save_q, tty, wait_Ram_q;
  wire [1:0] execute_select;

  Main_Decoder main_decoder_1 (
    .Input(in_1), .in_2(in_4), .in_3(Is_Inst), .out_4(out_8), .out_5(out_24), .out_6(out_22),
    .out_7(Mem_Read), .out_8(Mem_Write), .out_9(Is_Jump), .out_10(out_20), .out_11(is_RF), .out_12(out_18),
    .out_13(tty), .out_14(kbd), .out_15(halt), .out_16(out_12), .out_17(out_14), .out_18(out_16),
    .out_19(is_hi_lo), .out_20(out_10));
  or or_1 (or_1_out, demultiplexer_2_out0, in_5);
  Demultiplexer #(.enable("false")) demultiplexer_1 (.out0(get_data_2), .out1(out_9), .in(_mem), .sel(Mem_Write));
  or or_2 (Mem, Mem_Read, Mem_Write);
  not not_1 (not_1_out, in_5);
  or or_3 (or_3_out, demultiplexer_3_out0, _mem);
  or or_4 (out_7, get_data_2, get_data_1);
  and and_1 (out_19, out_11, kbd);
  nor nor_1 (is_PC, Mem, is_RF);
  D_Flip_Flop #(.trigger("falling")) Idle (.clk(in_2), .D(or_1_out), .Q(Idle_q));  // open: Qn, preset, en, reset
  Demultiplexer #(.enable("false")) demultiplexer_2 (
    .out0(demultiplexer_2_out0), .out1(demultiplexer_2_out1), .in(Idle_q), .sel(not_1_out));
  D_Flip_Flop #(.trigger("falling")) wait_Ram (
    .clk(in_2), .D(or_3_out), .Q(wait_Ram_q), .reset(in_5));  // open: Qn, preset, en
  or or_5 (get_data_1, out_11, demultiplexer_2_out1);
  Demultiplexer #(.enable("false")) demultiplexer_3 (
    .out0(demultiplexer_3_out0), .out1(demultiplexer_3_out1), .in(wait_Ram_q), .sel(multiplexer_1_out));
  Multiplexer #(.enable("false")) multiplexer_1 (.in0(in_3), .in1(in_6), .out(multiplexer_1_out), .sel(Mem_Write));
  Priority_Encoder #(.select(2)) priority_encoder_1 (
    .in0(is_RF), .in1(Mem), .in2(is_PC), .in3(halt), .out(execute_select), .en_in(1'b1));  // open: gs, en_out
  Demultiplexer #(.enable("false")) demultiplexer_4 (
    .out0(end_read), .out1(end_write), .in(demultiplexer_3_out1), .sel(Mem_Write));
  and and_2 (out_17, out_11, tty);
  and and_3 (out_21, out_11, is_hi_lo);
  or or_6 (Is_Inst, demultiplexer_5_out0, get_data_1);
  D_Flip_Flop #(.trigger("falling")) Fetch (
    .clk(in_2), .D(Is_Inst), .Q(Fetch_q), .reset(in_5));  // open: Qn, preset, en
  Demultiplexer #(.enable("false")) demultiplexer_5 (
    .out0(demultiplexer_5_out0), .out1(out_15), .in(Fetch_q), .sel(in_3));
  or or_7 (out_13, end_read, _RF);
  D_Flip_Flop #(.trigger("falling")) Save (.clk(in_2), .D(out_15), .Q(Save_q), .reset(in_5));  // open: Qn, preset, en
  D_Flip_Flop #(.trigger("falling")) Save_2 (
    .clk(in_2), .D(out_13), .Q(Save_2_q), .reset(in_5));  // open: Qn, preset, en
  Demultiplexer #(.select(2), .enable("false")) demultiplexer_6 (
    .out0(_RF), .out1(_mem), .out2(_pc), .out3(demultiplexer_6_out3), .in(Save_q), .sel(execute_select));
  or or_8 (out_23, End_q, demultiplexer_6_out3);
  or or_9 (out_11, Save_2_q, end_write, _pc);
  D_Flip_Flop #(.trigger("falling")) End (.clk(in_2), .D(out_23), .Q(End_q), .reset(in_5));  // open: Qn, preset, en

  assign out_25 = out_8;

  // Other names for the same wires on the sheet: ALU_Select[3:0] = out_22; BC_Select[1:0] = out_24; Clk = in_2;
  //   Const_extend = out_20; end = out_23; Func_Code[5:0] = in_4; get_data = out_7; HI_LO_en = out_21; IM_en = out_15;
  //   Jump_Cond[2:0] = out_8; kbd_en = out_19; Op_Code[5:0] = in_1; pop = out_12; push = out_14; Ready_R = in_3;
  //   Ready_W = in_6; reset = in_5; RF_en = out_13; RF_select[2:0] = out_18; sw = out_16; tty_en = out_17;
  //   HI_LO = out_11; Kbd_clear = out_11; next_inst = out_11; PC_en = out_11; tty_out = out_11; Type_I = out_10;
  //   write_data = out_9

  // Notes on the sheet:
  //   Input
  //   Output
endmodule

module ALU_Control (
  input  [5:0] Input,
  input  [5:0] in_2,
  output [3:0] out_3,
  output out_4,
  output out_5
);

  wire _00_0000, Add, add_t, addi, And, and_t, andi, comparator_1_eq, comparator_2_eq, comparator_3_eq,
       comparator_4_eq, comparator_5_eq, comparator_6_eq, comparator_12_eq, comparator_13_eq,
       comparator_14_eq, comparator_15_eq, comparator_16_eq, comparator_17_eq, div, divu, mult, mulu, \nor ,
       Or, or_t, ori, priority_encoder_1_gs, Slt, slt_t, slti, sltiu, Sltu, sltu_t, sub, Xor, xor_t, xori;
  wire [3:0] priority_encoder_1_out;

  Comparator #(.width(6)) comparator_1 (.a(in_2), .b(6'b100000), .eq(comparator_1_eq));  // open: gt, lt
  Comparator #(.width(6)) comparator_2 (.a(in_2), .b(6'b011010), .eq(comparator_2_eq));  // open: gt, lt
  Comparator #(.width(6)) comparator_3 (.a(in_2), .b(6'b100111), .eq(comparator_3_eq));  // open: gt, lt
  Comparator #(.width(6)) comparator_4 (.a(in_2), .b(6'b100010), .eq(comparator_4_eq));  // open: gt, lt
  Comparator #(.width(6)) comparator_5 (.a(in_2), .b(6'b011011), .eq(comparator_5_eq));  // open: gt, lt
  Comparator #(.width(6)) comparator_6 (.a(in_2), .b(6'b101000), .eq(comparator_6_eq));  // open: gt, lt
  Comparator #(.width(6)) comparator_7 (.a(Input), .b(6'b001000), .eq(addi));  // open: gt, lt
  Comparator #(.width(6)) comparator_8 (.a(Input), .b(6'b001010), .eq(slti));  // open: gt, lt
  and and_1 (add_t, _00_0000, comparator_1_eq);
  and and_2 (div, _00_0000, comparator_2_eq);
  and and_3 (\nor , _00_0000, comparator_3_eq);
  and and_4 (sub, _00_0000, comparator_4_eq);
  and and_5 (divu, _00_0000, comparator_5_eq);
  and and_6 (xor_t, _00_0000, comparator_6_eq);
  Comparator #(.width(6)) comparator_9 (.a(Input), .b(6'b001100), .eq(andi));  // open: gt, lt
  Comparator #(.width(6)) comparator_10 (.a(Input), .b(6'b001011), .eq(sltiu));  // open: gt, lt
  Comparator #(.width(6)) comparator_11 (.a(Input), .b({6{1'b0}}), .eq(_00_0000));  // open: gt, lt
  and and_7 (mult, _00_0000, comparator_12_eq);
  Comparator #(.width(6)) comparator_12 (.a(in_2), .b(6'b011000), .eq(comparator_12_eq));  // open: gt, lt
  and and_8 (and_t, _00_0000, comparator_13_eq);
  Comparator #(.width(6)) comparator_13 (.a(in_2), .b(6'b100100), .eq(comparator_13_eq));  // open: gt, lt
  and and_9 (slt_t, _00_0000, comparator_14_eq);
  Comparator #(.width(6)) comparator_14 (.a(in_2), .b(6'b101010), .eq(comparator_14_eq));  // open: gt, lt
  and and_10 (mulu, _00_0000, comparator_15_eq);
  Comparator #(.width(6)) comparator_15 (.a(in_2), .b(6'b011001), .eq(comparator_15_eq));  // open: gt, lt
  and and_11 (or_t, _00_0000, comparator_16_eq);
  Comparator #(.width(6)) comparator_16 (.a(in_2), .b(6'b100101), .eq(comparator_16_eq));  // open: gt, lt
  and and_12 (sltu_t, _00_0000, comparator_17_eq);
  Comparator #(.width(6)) comparator_17 (.a(in_2), .b(6'b101011), .eq(comparator_17_eq));  // open: gt, lt
  Comparator #(.width(6)) comparator_18 (.a(Input), .b(6'b001101), .eq(ori));  // open: gt, lt
  Comparator #(.width(6)) comparator_19 (.a(Input), .b(6'b001110), .eq(xori));  // open: gt, lt
  or or_1 (out_4, mult, mulu, div, divu);
  or or_2 (Add, add_t, addi);
  or or_3 (And, and_t, andi);
  or or_4 (Or, or_t, ori);
  Priority_Encoder #(.select(4)) priority_encoder_1 (
    .in0(Add), .in1(sub), .in2(Slt), .in3(Sltu), .in4(And), .in5(Or), .in6(\nor ), .in7(Xor), .in8(mult),
    .in9(mulu), .in10(div), .in11(divu), .out(priority_encoder_1_out), .gs(priority_encoder_1_gs),
    .en_in(1'b1));  // open: in12, in13, in14, in15, en_out
  Multiplexer #(.width(4), .enable("false")) multiplexer_1 (
    .in0(4'b0000), .in1(priority_encoder_1_out), .out(out_3), .sel(priority_encoder_1_gs));
  or or_5 (out_5, andi, xori, ori);
  or or_6 (Sltu, sltiu, sltu_t);
  or or_7 (Slt, slt_t, slti);
  or or_8 (Xor, xor_t, xori);

  // Other names for the same wires on the sheet: ALU_Selector[3:0] = out_3; Const_extend = out_5;
  //   Func_Code[5:0] = in_2; Hi_Lo = out_4; Op_Code[5:0] = Input

  // Notes on the sheet:
  //   Type I
  //   Type R
  //   HI Lo
  //   Output
  //   Const Extend
endmodule

module Type_I (
  input  [5:0] Input,
  output out_2
);

  wire _00_0000, _00_0010, _11_1000, _11_1111;

  Comparator #(.width(6)) comparator_1 (.a(Input), .b({6{1'b0}}), .eq(_00_0000));  // open: gt, lt
  Comparator #(.width(6)) comparator_2 (.a(Input), .b({6{1'b1}}), .eq(_11_1111));  // open: gt, lt
  Comparator #(.width(6)) comparator_3 (.a(Input), .b(6'b111000), .eq(_11_1000));  // open: gt, lt
  Comparator #(.width(6)) comparator_4 (.a(Input), .b(6'b000010), .eq(_00_0010));  // open: gt, lt
  nor nor_1 (out_2, _00_0000, _11_1111, _11_1000, _00_0010);

  // Other names for the same wires on the sheet: Op_Code[5:0] = Input; Type_I = out_2

  // Notes on the sheet:
  //   Output
endmodule

module BC_Selector (
  input  [5:0] Input,
  input  [5:0] in_2,
  output [2:0] out_3,
  output [1:0] out_4
);

  wire _00_0000, beq, bgtz, blez, bltz, bne, comparator_4_eq, IsBranch, j, jr;
  wire [2:0] priority_encoder_1_out;

  Comparator #(.width(6)) comparator_1 (.a(Input), .b(6'b000100), .eq(beq));  // open: gt, lt
  Comparator #(.width(6)) comparator_2 (.a(Input), .b(6'b000110), .eq(blez));  // open: gt, lt
  Comparator #(.width(6)) comparator_3 (.a(Input), .b(6'b000001), .eq(bltz));  // open: gt, lt
  Comparator #(.width(6)) comparator_4 (.a(in_2), .b(6'b001000), .eq(comparator_4_eq));  // open: gt, lt
  Comparator #(.width(6)) comparator_5 (.a(Input), .b(6'b000101), .eq(bne));  // open: gt, lt
  Comparator #(.width(6)) comparator_6 (.a(Input), .b(6'b000111), .eq(bgtz));  // open: gt, lt
  Comparator #(.width(6)) comparator_7 (.a(Input), .b(6'b000010), .eq(j));  // open: gt, lt
  and and_1 (jr, _00_0000, comparator_4_eq);
  Comparator #(.width(6)) comparator_8 (.a(Input), .b({6{1'b0}}), .eq(_00_0000));  // open: gt, lt
  Priority_Encoder priority_encoder_1 (
    .in0(beq), .in1(bne), .in2(bgtz), .in3(blez), .in4(bltz), .out(priority_encoder_1_out), .en_in(1'b1),
    .gs(IsBranch));  // open: in5, in6, in7, en_out
  or or_1 (out_4[0], IsBranch, jr);
  or or_2 (out_4[1], jr, j);
  Multiplexer #(.width(3), .enable("false")) multiplexer_1 (
    .in0(3'b000), .in1(priority_encoder_1_out), .out(out_3), .sel(IsBranch));

  // Other names for the same wires on the sheet: BC_Selector[1:0] = out_4; Func_Code[5:0] = in_2;
  //   Jump_Condition[2:0] = out_3; Op_Code[5:0] = Input

  // Notes on the sheet:
  //   Output
endmodule

module Program_Counter (
  input  in_1,
  input  in_2,
  input  in_3,
  input  [31:0] in_4,
  output [31:0] out_5
);

  Register #(.width(32)) register_1 (.D(in_4), .en(in_2), .Q(out_5), .clk(in_1), .clr(in_3));

  // Other names for the same wires on the sheet: Clock = in_1; Enable = in_2; Reset = in_3
endmodule

module Branch_Control (
  input  [31:0] in_1,
  input  [31:0] in_2,
  input  [31:0] in_3,
  input  [25:0] in_4,
  input  [1:0] in_5,
  input  [2:0] in_6,
  input  [15:0] in_7,
  output [31:0] out_8
);

  wire comparator_2_eq, multiplexer_2_out, tunnel, tunnel_t, tunnel_t_t, tunnel_t_t_t, tunnel_t_t_t_t;
  wire [13:0] bit_extender_1_out;
  wire [31:0] multiplexer_1_out, PC___4, PC___4___4_x_Offset;

  Adder #(.width(32)) adder_1 (.a(in_3), .b(32'h4), .out(PC___4));  // open: cin, cout
  assign bit_extender_1_out = {{13{in_7[15]}}, in_7[15]};  // Bit_Extender bit_extender_1
  Adder #(.width(32)) adder_2 (
    .a(PC___4), .b({bit_extender_1_out, in_7, 2'b00}), .out(PC___4___4_x_Offset));  // open: cin, cout
  Comparator #(.width(32)) comparator_1 (.a(in_1), .b(in_2), .eq(tunnel_t_t_t));  // open: gt, lt
  Comparator #(.width(32)) comparator_2 (
    .a(in_1), .b({32{1'b0}}), .gt(tunnel_t_t_t_t), .eq(comparator_2_eq), .lt(tunnel_t));
  not not_1 (tunnel, tunnel_t_t_t);
  or or_1 (tunnel_t_t, comparator_2_eq, tunnel_t);
  Multiplexer #(.width(32), .enable("false")) multiplexer_1 (
    .in0(PC___4), .in1(PC___4___4_x_Offset), .out(multiplexer_1_out), .sel(multiplexer_2_out));
  Multiplexer #(.select(3), .enable("false")) multiplexer_2 (
    .in0(tunnel_t_t_t), .in1(tunnel), .in2(tunnel_t_t_t_t), .in3(tunnel_t_t), .in4(tunnel_t),
    .out(multiplexer_2_out), .sel(in_6));  // open: in5, in6, in7
  Multiplexer #(.select(2), .width(32), .enable("false")) multiplexer_3 (
    .in0(PC___4), .in1(multiplexer_1_out), .in2({in_3[31:28], in_4, 2'b00}), .in3(in_1), .out(out_8),
    .sel(in_5));

  // Other names for the same wires on the sheet: Offset[15:0] = in_7; Branch_Selector[1:0] = in_5;
  //   Destiny[25:0] = in_4; Jump[31:2] = {in_3[31:28], in_4}; PC[31:0] = in_3; Jump_Condition[2:0] = in_6;
  //   PC_Input[31:0] = out_8; RS[31:0] = in_1; RT[31:0] = in_2

  // Notes on the sheet:
  //   Input
  //   Output
endmodule

module Main_Decoder (
  input  [5:0] Input,
  input  [5:0] in_2,
  input  in_3,
  output [2:0] out_4,
  output [1:0] out_5,
  output [3:0] out_6,
  output out_7,
  output out_8,
  output out_9,
  output out_10,
  output out_11,
  output [2:0] out_12,
  output out_13,
  output out_14,
  output out_15,
  output out_16,
  output out_17,
  output out_18,
  output out_19,
  output out_20
);

  wire _00_0000, _11_1000, _11_1111, comparator_3_eq, comparator_6_eq, comparator_7_eq, comparator_9_eq,
       comparator_10_eq, lw, nor_1_out;
  wire [1:0] MA_Selector;

  BC_Selector bc_selector_1 (.Input(Input), .in_2(in_2), .out_3(out_4), .out_4(out_5));
  ALU_Control alu_control_1 (.Input(Input), .in_2(in_2), .out_3(out_6), .out_4(out_19), .out_5(out_10));
  Comparator #(.width(6)) comparator_1 (.a(Input), .b({6{1'b1}}), .eq(_11_1111));  // open: gt, lt
  Comparator #(.width(6)) comparator_2 (.a(Input), .b(6'b111000), .eq(_11_1000));  // open: gt, lt
  Comparator #(.width(6)) comparator_3 (.a(in_2), .b({6{1'b1}}), .eq(comparator_3_eq));  // open: gt, lt
  Comparator #(.width(6)) comparator_4 (.a(Input), .b(6'b100011), .eq(lw));  // open: gt, lt
  and and_1 (out_15, _11_1111, comparator_3_eq);
  Type_I type_i_1 (.Input(Input), .out_2(out_20));
  Mem_R_W mem_r_w_1 (
    .out_6(out_7), .out_7(out_8), .in_5(in_3), .out_8(MA_Selector), .in_1(out_16), .in_4(lw), .in_3(out_18),
    .in_2(out_17));
  Comparator #(.width(6)) comparator_5 (.a(Input), .b({6{1'b0}}), .eq(_00_0000));  // open: gt, lt
  and and_2 (out_13, _11_1111, comparator_6_eq);
  Comparator #(.width(6)) comparator_6 (.a(in_2), .b(6'b000001), .eq(comparator_6_eq));  // open: gt, lt
  Comparator #(.width(6)) comparator_7 (.a(in_2), .b(6'b000100), .eq(comparator_7_eq));  // open: gt, lt
  Comparator #(.width(6)) comparator_8 (.a(Input), .b(6'b101011), .eq(out_18));  // open: gt, lt
  and and_3 (out_14, _11_1111, comparator_7_eq);
  nor nor_1 (nor_1_out, out_9, out_7, out_8);
  Is_Jump is_jump_1 (.BC_Selector(out_5), .out_2(out_9));
  Is_RF is_rf_1 (
    .in_1(Input), .in_2(nor_1_out), .in_3(in_2), .in_4(out_19), .in_5(lw), .in_6(out_15), .in_7(out_16),
    .in_8(out_14), .in_9(out_13), .out_10(out_11), .out_11(out_12));
  Comparator #(.width(6)) comparator_9 (.a(in_2), .b({6{1'b0}}), .eq(comparator_9_eq));  // open: gt, lt
  Comparator #(.width(6)) comparator_10 (.a(in_2), .b(6'b000001), .eq(comparator_10_eq));  // open: gt, lt
  and and_4 (out_16, comparator_9_eq, _11_1000);
  and and_5 (out_17, _11_1000, comparator_10_eq);

  // Other names for the same wires on the sheet: ALU_Selector[3:0] = out_6; BC_Selector[1:0] = out_5;
  //   Const_Extend = out_10; Func_Code[5:0] = in_2; halt = out_15; Hi_Lo = out_19; Is_Inst = in_3; Is_Jump = out_9;
  //   Is_RF = out_11; Jump_Condition[2:0] = out_4; kbd = out_14; Mem_Read = out_7; Mem_Write = out_8;
  //   Op_Code[5:0] = Input; pop = out_16; push = out_17; RF_Selector[2:0] = out_12; sw = out_18; tty = out_13;
  //   Type_I = out_20

  // Notes on the sheet:
  //   Main Decoder
  //   CU Flags
  //   Output
endmodule

module Mem_R_W (
  input  in_1,
  input  in_2,
  input  in_3,
  input  in_4,
  input  in_5,
  output out_6,
  output out_7,
  output [1:0] out_8
);

  or or_1 (out_6, in_1, in_3);
  or or_2 (out_7, in_4, in_2);
  or or_3 (out_8[0], in_1, in_5, in_2);
  or or_4 (out_8[1], in_4, in_5, in_3);

  // Other names for the same wires on the sheet: Is_Instruction = in_5; lw = in_3; MA_Selector[1:0] = out_8;
  //   Mem_Read = out_6; Mem_Write = out_7; pop = in_1; push = in_2; sw = in_4

  // Notes on the sheet:
  //   Input
  //   Output
endmodule

module Is_Jump (
  input  [1:0] BC_Selector,
  output out_2
);

  or or_1 (out_2, BC_Selector[0], BC_Selector[1]);

  // Notes on the sheet:
  //   Is Jump
endmodule

module Is_RF (
  input  [5:0] in_1,
  input  in_2,
  input  [5:0] in_3,
  input  in_4,
  input  in_5,
  input  in_6,
  input  in_7,
  input  in_8,
  input  in_9,
  output out_10,
  output [2:0] out_11
);

  wire _00_0000, _11_1000, _11_1111, comparator_1_eq, comparator_2_eq, comparator_6_eq, comparator_7_eq,
       Is_RAM, mfhi, mflo, nop, nor_1_out, or_1_out, priority_encoder_1_gs, rnd;
  wire [2:0] priority_encoder_1_out;

  Comparator #(.width(6)) comparator_1 (.a(in_3), .b(6'b010000), .eq(comparator_1_eq));  // open: gt, lt
  Comparator #(.width(6)) comparator_2 (.a(in_3), .b(6'b000010), .eq(comparator_2_eq));  // open: gt, lt
  Comparator #(.width(6)) comparator_3 (.a(in_1), .b({6{1'b1}}), .eq(_11_1111));  // open: gt, lt
  and and_1 (mfhi, _00_0000, comparator_1_eq);
  and and_2 (rnd, _11_1111, comparator_2_eq);
  Comparator #(.width(6)) comparator_4 (.a(in_1), .b(6'b111000), .eq(_11_1000));  // open: gt, lt
  Comparator #(.width(6)) comparator_5 (.a(in_1), .b({6{1'b0}}), .eq(_00_0000));  // open: gt, lt
  Comparator #(.width(6)) comparator_6 (.a(in_3), .b(6'b010010), .eq(comparator_6_eq));  // open: gt, lt
  Comparator #(.width(6)) comparator_7 (.a(in_3), .b({6{1'b0}}), .eq(comparator_7_eq));  // open: gt, lt
  and and_3 (mflo, _00_0000, comparator_6_eq);
  and and_4 (nop, _00_0000, comparator_7_eq);
  or or_1 (or_1_out, in_2, in_8, rnd, mflo, mfhi);
  nor nor_1 (nor_1_out, in_4, in_6, nop, in_9);
  or or_2 (Is_RAM, in_5, in_7);
  Priority_Encoder priority_encoder_1 (
    .in1(in_8), .in2(rnd), .in3(Is_RAM), .in4(mfhi), .in5(mflo), .out(priority_encoder_1_out), .en_in(1'b1),
    .gs(priority_encoder_1_gs));  // open: in0, in6, in7, en_out
  Multiplexer #(.width(3), .enable("false")) multiplexer_1 (
    .in0(3'b000), .in1(priority_encoder_1_out), .out(out_11), .sel(priority_encoder_1_gs));
  and and_5 (out_10, or_1_out, nor_1_out);

  // Other names for the same wires on the sheet: Func_Code[5:0] = in_3; halt = in_6; Hi_Lo = in_4; Is_RF = out_10;
  //   kbd = in_8; lw = in_5; nrwj = in_2; Op_Code[5:0] = in_1; pop = in_7; RF_Selector[2:0] = out_11; tty = in_9

  // Notes on the sheet:
  //   Input
  //   Output
endmodule
