// Logisim project Data Path.circ as structural Verilog: 6 circuits, main circuit Data Path
module Data_Path (
  input  [6:0] in_1,
  input  [31:0] in_2,
  input  [15:0] in_3,
  input  [2:0] in_4,
  input  [25:0] in_5,
  input  [1:0] in_6,
  input  in_7,
  input  in_8,
  input  in_9,
  input  in_10,
  input  in_11,
  input  in_12,
  input  in_13,
  input  in_14,
  input  [4:0] in_15,
  input  [3:0] in_16,
  input  [4:0] in_17,
  input  in_18,
  input  [4:0] in_19,
  input  in_20,
  input  [2:0] in_21,
  input  in_22,
  output [31:0] out_23,
  output [31:0] out_24,
  output [31:0] out_25,
  output [31:0] out_26,
  output [31:0] out_27,
  output [31:0] out_28,
  output [6:0] out_29
);

  wire [4:0] Data_Address;
  wire [31:0] alu_input_1_out_5, ALU_out_t, branch_control_1_out_8, Hgih_out, High_in, Low_out, Ram__write,
       rf_input_1_rf_input, RT_t;
  wire [31:7] RS_t;

  Multiplexer #(.width(5), .enable("false")) multiplexer_1 (.in0(in_15), .in1(in_19), .out(Data_Address), .sel(in_14));
  ALU_Input alu_input_1 (.in_1(RT_t), .in_2(in_3), .in_3(in_18), .in_4(in_14), .out_5(alu_input_1_out_5));
  Branch_Control branch_control_1 (
    .in_1({RS_t, out_29}), .in_2(RT_t), .in_3(out_28), .in_4(in_5), .in_5(in_6), .in_6(in_4), .in_7(in_3),
    .out_8(branch_control_1_out_8));
  RF_Input rf_input_1 (
    .in_1(in_21), .in_2(in_2), .in_3(ALU_out_t), .in_4(Hgih_out), .Kbd(in_1), .in_6(Low_out), .in_7(in_20),
    .in_8(in_13), .RF_Input(rf_input_1_rf_input));
  Program_Counter program_counter_1 (
    .in_1(in_20), .in_2(in_10), .in_3(in_22), .in_4(branch_control_1_out_8), .out_5(out_28));
  ALU alu_1 (.in_1({RS_t, out_29}), .in_2(alu_input_1_out_5), .Operation(in_16), .out_4(High_in), .out_5(ALU_out_t));
  Multiplexer #(.width(32), .enable("false")) multiplexer_2 (
    .in0({RS_t, out_29}), .in1(RT_t), .out(Ram__write), .sel(in_12));
  // Register_file register_file_1: pin names not known; wires that end beside it: rf_input_1_rf_input, Data_Address, in_17, in_19, in_8, in_7, in_11, in_20, in_22, in_10, {RS_t, out_29}, RT_t, out_26
  // HILO hilo_1: pin names not known; wires that end beside it: ALU_out_t, High_in, in_20, in_9, Low_out, Hgih_out

  // Other names for the same wires on the sheet: A_Selector[4:0] = in_17; ALU_Out[31:0] = out_24;
  //   ALU_Selector[3:0] = in_16; B_Selector[4:0] = in_19; BC_Selector[1:0] = in_6; Clk = in_20; Const[15:0] = in_3;
  //   Const_Extend = in_18; Destiny[25:0] = in_5; Hi_Lo_en = in_9; Jump_Condition[2:0] = in_4; kbd_Data[6:0] = in_1;
  //   kbd_en = in_13; PC_en = in_10; PC_Output[31:0] = out_28; pop = in_8; push = in_7; R_W_en = in_11;
  //   RAM_Data[31:0] = in_2; RAM_Write_Data[31:0] = out_23; RD[4:0] = in_15; Reset = in_22; RF_Selector[2:0] = in_21;
  //   RS[31:0] = out_25; RS_t[6:0] = out_29; tty_Data[6:0] = out_29; RT[31:0] = out_27; SP[31:0] = out_26; sw = in_12;
  //   Type_I = in_14

  // Notes on the sheet:
  //   Input
  //   Output
  //   Data Path
endmodule

module Branch_Control (
  input  [31:0] in_1,
  input  [31:0] in_2,
  input  [31:0] in_3,
  input  [25:0] in_4,
  input  [1:0] in_5,
  input  [2:0] in_6,
  input  [15:0] in_7,
  output [31:0] out_8
);

  wire comparator_2_eq, multiplexer_2_out, tunnel, tunnel_t, tunnel_t_t, tunnel_t_t_t, tunnel_t_t_t_t;
  wire [13:0] bit_extender_1_out;
  wire [31:0] multiplexer_1_out, PC___4, PC___4___4_x_Offset;

  Adder #(.width(32)) adder_1 (.a(in_3), .b(32'h4), .out(PC___4));  // open: cin, cout
  assign bit_extender_1_out = {{13{in_7[15]}}, in_7[15]};  // Bit_Extender bit_extender_1
  Adder #(.width(32)) adder_2 (
    .a(PC___4), .b({bit_extender_1_out, in_7, 2'b00}), .out(PC___4___4_x_Offset));  // open: cin, cout
  Comparator #(.width(32)) comparator_1 (.a(in_1), .b(in_2), .eq(tunnel_t_t_t));  // open: gt, lt
  Comparator #(.width(32)) comparator_2 (
    .a(in_1), .b({32{1'b0}}), .gt(tunnel_t_t_t_t), .eq(comparator_2_eq), .lt(tunnel_t));
  not not_1 (tunnel, tunnel_t_t_t);
  or or_1 (tunnel_t_t, comparator_2_eq, tunnel_t);
  Multiplexer #(.width(32), .enable("false")) multiplexer_1 (
    .in0(PC___4), .in1(PC___4___4_x_Offset), .out(multiplexer_1_out), .sel(multiplexer_2_out));
  Multiplexer #(.select(3), .enable("false")) multiplexer_2 (
    .in0(tunnel_t_t_t), .in1(tunnel), .in2(tunnel_t_t_t_t), .in3(tunnel_t_t), .in4(tunnel_t),
    .out(multiplexer_2_out), .sel(in_6));  // open: in5, in6, in7
  Multiplexer #(.select(2), .width(32), .enable("false")) multiplexer_3 (
    .in0(PC___4), .in1(multiplexer_1_out), .in2({in_3[31:28], in_4, 2'b00}), .in3(in_1), .out(out_8),
    .sel(in_5));

  // Other names for the same wires on the sheet: Offset[15:0] = in_7; Branch_Selector[1:0] = in_5;
  //   Destiny[25:0] = in_4; Jump[31:2] = {in_3[31:28], in_4}; PC[31:0] = in_3; Jump_Condition[2:0] = in_6;
  //   PC_Input[31:0] = out_8; RS[31:0] = in_1; RT[31:0] = in_2

  // Notes on the sheet:
  //   Input
  //   Output
endmodule

module Program_Counter (
  input  in_1,
  input  in_2,
  input  in_3,
  input  [31:0] in_4,
  output [31:0] out_5
);

  Register #(.width(32)) register_1 (.D(in_4), .en(in_2), .Q(out_5), .clk(in_1), .clr(in_3));

  // Other names for the same wires on the sheet: Clock = in_1; Enable = in_2; Reset = in_3
endmodule

module ALU_Input (
  input  [31:0] in_1,
  input  [15:0] in_2,
  input  in_3,
  input  in_4,
  output [31:0] out_5
);

  wire [31:0] New_Const;

  Multiplexer #(.width(32), .enable("false")) multiplexer_1 (.in0(in_1), .in1(New_Const), .out(out_5), .sel(in_4));
  Const_Extender const_extender_1 (.in_1(in_3), .in_2(in_2), .out_3(New_Const));

  // Other names for the same wires on the sheet: Const[15:0] = in_2; Const_Extender_Selector = in_3;
  //   Data_Out[31:0] = out_5; RT[31:0] = in_1; Type_I = in_4

  // Notes on the sheet:
  //   Input
  //   Output
endmodule

module Const_Extender (
  input  in_1,
  input  [15:0] in_2,
  output [31:0] out_3
);

  wire and_1_out;

  and and_1 (and_1_out, ~in_1, in_2[15]);  // AND_Gate
  assign out_3 = {{16{and_1_out}}, in_2};  // Bit_Extender bit_extender_1

  // Other names for the same wires on the sheet: Const[15:0] = in_2; Bit_15 = in_2[15];
  //   Const_Extender_Selector = in_1; Const_Out[31:0] = out_3

  // Notes on the sheet:
  //   Constant Extender
endmodule

module RF_Input (
  input  [2:0] in_1,
  input  [31:0] in_2,
  input  [31:0] in_3,
  input  [31:0] in_4,
  input  [6:0] Kbd,
  input  [31:0] in_6,
  input  in_7,
  input  in_8,
  output [31:0] RF_Input
);

  wire [31:0] kbd_input, Random_out;

  Random #(.width(32)) Random (.clk(in_7), .out(Random_out));  // open: next, clr
  Multiplexer #(.width(32), .enable("false")) multiplexer_1 (
    .in0({32{1'b1}}), .in1({{25{1'b0}}, Kbd}), .out(kbd_input), .sel(in_8));
  Multiplexer #(.select(3), .width(32), .enable("false")) multiplexer_2 (
    .in0(in_3), .in1(kbd_input), .in2(Random_out), .in3(in_2), .in4(in_4), .in5(in_6), .out(RF_Input),
    .sel(in_1));  // open: in6, in7

  // Other names for the same wires on the sheet: ALU_Output[31:0] = in_3; Clk = in_7; High[31:0] = in_4;
  //   kbd_avail = in_8; kbd_t[6:0] = Kbd; Low[31:0] = in_6; RAM[31:0] = in_2; RF_Select[2:0] = in_1

  // Notes on the sheet:
  //   Register File Input
endmodule
