// Logisim project Instruction Memory.circ as structural Verilog: 1 circuit, main circuit Instruction Memory
module Instruction_Memory (
  input  [31:0] in_1,
  input  en,
  input  Clk,
  input  Reset,
  output [31:0] out_5
);

  Register #(.width(32)) register_1 (.D(in_1), .en(en), .Q(out_5), .clk(Clk), .clr(Reset));

  // Notes on the sheet:
  //   Instruction Memory
endmodule
