// Logisim project Memory Address.circ as structural Verilog: 1 circuit, main circuit Memory Address
module Memory_Address (
  input  [31:0] ALU,
  input  [31:0] SP,
  input  [1:0] in_3,
  input  [31:0] PC,
  input  in_5,
  output [31:0] RAM_dir
);

  wire [31:0] multiplexer_1_out, subtractor_1_out;

  Subtractor #(.width(32)) subtractor_1 (.a(SP), .b(32'h4), .out(subtractor_1_out));  // open: bin, bout
  Multiplexer #(.width(32), .enable("false")) multiplexer_1 (
    .in0(SP), .in1(subtractor_1_out), .out(multiplexer_1_out), .sel(in_5));
  Multiplexer #(.select(2), .width(32), .enable("false")) multiplexer_2 (
    .in1(ALU), .in2(multiplexer_1_out), .in3(PC), .out(RAM_dir), .sel(in_3));  // open: in0

  // Other names for the same wires on the sheet: push = in_5; selector[1:0] = in_3

  // Notes on the sheet:
  //   Memory Address
endmodule
