// Logisim project RAM Query.circ as structural Verilog: 5 circuits, main circuit RAM Query
module RAM_Query (
  input  [31:0] in_1,
  input  [31:0] in_2,
  input  [31:0] in_3,
  input  [31:0] in_4,
  input  miss,
  input  [31:0] in_6,
  input  [3:0] in_7,
  input  in_8,
  input  in_9,
  input  [31:0] in_10,
  input  [3:0] in_11,
  input  in_12,
  input  in_13,
  output [31:0] out_14,
  output [31:0] out_15,
  output [31:0] out_16,
  output [31:0] out_17,
  output out_18,
  output out_19,
  output [31:0] out_20,
  output [3:0] out_21,
  output out_22,
  output out_23,
  output [15:0] out_24,
  output out_25,
  output out_26
);

  wire CSR;

  Read_Data read_data_1 (
    .bank0(in_1), .bank1(in_2), .bank2(in_3), .bank3(in_4), .in_5(in_8), .Ram_Dir(in_6), .RT(in_7),
    .in_9(in_12), .in_10(in_13), .out_12(CSR), .out_14(out_22), .read_data(out_20), .miss(miss),
    .GETCACHE(out_19));
  Write_Data write_data_1 (
    .in_1(in_6), .in_2(in_10), .in_3(in_8), .in_4(in_11), .in_5(in_12), .in_6(in_9), .out_8(out_14),
    .out_9(out_15), .out_10(out_16), .out_11(out_17), .out_12(out_26), .out_13(out_25), .Write_Cache(out_18));
  Demultiplexer #(.select(2), .enable("false")) demultiplexer_1 (
    .out0(out_21[0]), .out1(out_21[1]), .out2(out_21[2]), .out3(out_21[3]), .in(1'b1), .sel(in_6[3:2]));
  or or_1 (out_23, CSR, out_26);

  assign out_24 = in_6[19:4];

  // Other names for the same wires on the sheet: clk = in_8; CS = out_23; data_in[31:0] = in_10;
  //   data_out[31:0] = out_20; DR[31:0] = in_6; Address[15:0] = in_6[19:4]; get = in_13; mask[3:0] = out_21;
  //   CSW = out_26; R_W = out_26; Read_Cache = out_19; Read_Time[3:0] = in_7; ready_data = out_22;
  //   ready_write = out_25; Ri0[31:0] = out_14; Ri1[31:0] = out_15; Ri2[31:0] = out_16; Ri3[31:0] = out_17;
  //   RO0[31:0] = in_1; RO1[31:0] = in_2; RO2[31:0] = in_3; RO3[31:0] = in_4; rst = in_12; write = in_9;
  //   Write_Cache = out_18; Write_Time[3:0] = in_11

  // Notes on the sheet:
  //   Input
  //   Output
endmodule

module Timer (
  input  in_1,
  input  in_2,
  input  in_3,
  input  [3:0] in_4,
  output out_5
);

  wire [3:0] counter_1_q;

  Counter #(.width(4), .max('hf)) counter_1 (
    .count(in_1), .Q(counter_1_q), .clk(in_3), .clr(in_2));  // open: load, D, carry
  Comparator #(.width(4)) comparator_1 (.a(in_4), .b(counter_1_q), .eq(out_5));  // open: gt, lt

  // Other names for the same wires on the sheet: clk = in_3; ready = out_5; reset = in_2; start = in_1;
  //   wait_time[3:0] = in_4

  // Notes on the sheet:
  //   Timer
endmodule

module Inverse (
  input  [31:0] in_1,
  output [31:0] out_2
);


  assign out_2 = {in_1[7:0], in_1[15:8], in_1[23:16], in_1[31:24]};

  // Notes on the sheet:
  //   Bytes Inverser
endmodule

module Read_Data (
  input  [31:0] bank0,
  input  [31:0] bank1,
  input  [31:0] bank2,
  input  [31:0] bank3,
  input  in_5,
  input  miss,
  input  [31:0] Ram_Dir,
  input  [3:0] RT,
  input  in_9,
  input  in_10,
  output GETCACHE,
  output out_12,
  output [31:0] read_data,
  output out_14
);

  wire d_ff_2_q, demultiplexer_1_out0, demultiplexer_1_out1, or_1_out, or_2_out, or_3_out, or_4_out, ready;
  wire [31:0] inverse_1_out_2, multiplexer_1_out;

  or or_1 (or_1_out, out_14, in_9);
  Timer timer_1 (.in_1(GETCACHE), .in_2(or_1_out), .in_3(in_5), .out_5(ready), .in_4(RT));
  or or_2 (or_2_out, demultiplexer_1_out0, in_10);
  D_Flip_Flop d_ff_1 (.clk(in_5), .D(or_2_out), .Q(GETCACHE), .reset(in_9));  // open: Qn, preset, en
  Multiplexer #(.select(2), .width(32), .enable("false")) multiplexer_1 (
    .in0(bank0), .in1(bank1), .in2(bank2), .in3(bank3), .out(multiplexer_1_out), .sel(Ram_Dir[3:2]));
  Demultiplexer #(.enable("false")) demultiplexer_1 (
    .out0(demultiplexer_1_out0), .out1(demultiplexer_1_out1), .in(GETCACHE), .sel(or_3_out));
  D_Flip_Flop d_ff_2 (.clk(in_5), .D(miss), .Q(d_ff_2_q), .reset(in_9));  // open: Qn, preset, en
  Inverse inverse_1 (.in_1(multiplexer_1_out), .out_2(inverse_1_out_2));
  or or_3 (or_3_out, ~or_4_out, ready);  // OR_Gate
  or or_4 (or_4_out, d_ff_2_q, miss);
  Register #(.width(32)) register_1 (.D(inverse_1_out_2), .en(GETCACHE), .Q(read_data), .clk(in_5), .clr(in_9));
  D_Flip_Flop d_ff_3 (.clk(in_5), .D(demultiplexer_1_out1), .Q(out_14), .reset(in_9));  // open: Qn, preset, en

  assign out_12 = GETCACHE;

  // Other names for the same wires on the sheet: Clk = in_5; CS = GETCACHE; data[31:0] = read_data; get = in_10;
  //   Selector[1:0] = Ram_Dir[3:2]; Read_Time[3:0] = RT; ready_read = out_14; reset = in_9

  // Notes on the sheet:
  //   Input
  //   Output
  //   RAM Reader
endmodule

module Write_Data (
  input  [31:0] in_1,
  input  [31:0] in_2,
  input  in_3,
  input  [3:0] in_4,
  input  in_5,
  input  in_6,
  output Write_Cache,
  output [31:0] out_8,
  output [31:0] out_9,
  output [31:0] out_10,
  output [31:0] out_11,
  output out_12,
  output out_13
);

  wire demultiplexer_1_out0, demultiplexer_1_out1, or_1_out, or_2_out, Ready;
  wire [31:0] inverse_1_out_2;

  or or_1 (or_1_out, demultiplexer_1_out0, in_6);
  D_Flip_Flop d_ff_1 (.clk(in_3), .D(or_1_out), .Q(out_12), .reset(in_5));  // open: Qn, preset, en
  or or_2 (or_2_out, in_5, out_13);
  Demultiplexer #(.enable("false")) demultiplexer_1 (
    .out0(demultiplexer_1_out0), .out1(demultiplexer_1_out1), .in(out_12), .sel(Ready));
  Timer timer_1 (.in_1(out_12), .in_2(or_2_out), .in_3(in_3), .out_5(Ready), .in_4(in_4));
  Inverse inverse_1 (.in_1(in_2), .out_2(inverse_1_out_2));
  D_Flip_Flop d_ff_2 (.clk(in_3), .D(demultiplexer_1_out1), .Q(out_13), .reset(in_5));  // open: Qn, preset, en
  Demultiplexer #(.select(2), .width(32), .enable("false")) demultiplexer_2 (
    .out0(out_8), .out1(out_9), .out2(out_10), .out3(out_11), .in(inverse_1_out_2), .sel(in_1[3:2]));

  assign Write_Cache = out_12;

  // Other names for the same wires on the sheet: Bank0[31:0] = out_8; Bank1[31:0] = out_9; Bank2[31:0] = out_10;
  //   Bank3[31:0] = out_11; Clk = in_3; RAM_Dir[1:0] = in_1[3:2]; R_W = out_12; Ready_Write = out_13; Reset = in_5;
  //   Value[31:0] = in_2; Write = in_6; Write_Time[3:0] = in_4

  // Notes on the sheet:
  //   Input
  //   Output
  //   RAM Writer
endmodule
