// Logisim project cache.circ as structural Verilog: 2 circuits, main circuit cache
module cache (
  input  [1:0] PC_en,
  input  PC,
  input  Write,
  input  Write_Value,
  input  [31:0] DIR,
  input  CS,
  input  in_7,
  input  in_8,
  input  [31:0] D1,
  input  [31:0] D2,
  input  [31:0] D3,
  input  [31:0] D4,
  input  Read,
  input  [31:0] Value,
  output out_15,
  output [31:0] DataOut,
  output out_17
);

  wire AC1, AC2, AC3, AC4, and_2_out, comparator_1_eq, not_1_out, not_2_out, or_1_out, or_2_out, V1, V2, V3,
       V4, W1, W2, W3, W4;
  wire [1:0] index, offset, priority_encoder_1_out;
  wire [2:0] counter_1_q;
  wire [31:0] B1, B2, B3, B4, D1_t, D2_t, D3_t, D4_t, multiplexer_1_out, RAM_DIR;

  or or_1 (or_1_out, PC_en[0], PC_en[1]);
  not not_1 (not_1_out, in_8);
  and and_1 (out_15, PC, or_1_out);
  Demultiplexer #(.select(2), .enable("false")) demultiplexer_1 (
    .out0(W1), .out1(W2), .out2(W3), .out3(W4), .in(Write), .sel(index));
  Counter #(.width(3), .max('h7), .trigger("falling")) counter_1 (
    .count(not_1_out), .Q(counter_1_q), .clk(Write), .clr(or_2_out));  // open: load, D, carry
  or or_2 (or_2_out, comparator_1_eq, in_8);
  Register #(.width(32), .trigger("high")) register_1 (
    .D(DIR), .en(or_1_out), .Q({RAM_DIR[31:6], index, offset, RAM_DIR[1:0]}), .clk(in_7));  // open: clr
  Register #(.width(32)) register_2 (.D(D1), .en(CS), .Q(D1_t), .clk(in_7));  // open: clr
  Register #(.width(32)) register_3 (.D(D2), .en(CS), .Q(D2_t), .clk(in_7));  // open: clr
  Register #(.width(32)) register_4 (.D(D3), .en(CS), .Q(D3_t), .clk(in_7));  // open: clr
  Register #(.width(32)) register_5 (.D(D4), .en(CS), .Q(D4_t), .clk(in_7));  // open: clr
  Comparator #(.width(3)) comparator_1 (.a(counter_1_q), .b(3'b100), .eq(comparator_1_eq));  // open: gt, lt
  Demultiplexer #(.select(2), .enable("false")) demultiplexer_2 (
    .out0(W1), .out1(W2), .out2(W3), .out3(W4), .in(Write_Value), .sel(index));
  Demultiplexer #(.select(2), .enable("false")) demultiplexer_3 (
    .out0(AC1), .out1(AC2), .out2(AC3), .out3(AC4), .in(Read), .sel(index));
  line line_1 (
    .Tag(RAM_DIR[17:6]), .offset(offset), .Write(W1), .clock(in_7), .reset(in_8), .out_14(B1), .out_15(V1),
    .in_9(D1_t), .in_10(D2_t), .in_11(D3_t), .in_12(D4_t), .Read(Read), .ACt(AC1), .Write_Value(Write_Value),
    .Value(Value));
  line line_2 (
    .Tag(RAM_DIR[17:6]), .offset(offset), .Write(W2), .clock(in_7), .reset(in_8), .out_14(B2), .out_15(V2),
    .in_9(D1_t), .in_10(D2_t), .in_11(D3_t), .in_12(D4_t), .Read(Read), .ACt(AC2), .Write_Value(Write_Value),
    .Value(Value));
  line line_3 (
    .Tag(RAM_DIR[17:6]), .offset(offset), .Write(W3), .clock(in_7), .reset(in_8), .out_14(B3), .out_15(V3),
    .in_9(D1_t), .in_10(D2_t), .in_11(D3_t), .in_12(D4_t), .Read(Read), .ACt(AC3), .Write_Value(Write_Value),
    .Value(Value));
  line line_4 (
    .Tag(RAM_DIR[17:6]), .offset(offset), .Write(W4), .clock(in_7), .reset(in_8), .out_14(B4), .out_15(V4),
    .in_9(D1_t), .in_10(D2_t), .in_11(D3_t), .in_12(D4_t), .Read(Read), .ACt(AC4), .Write_Value(Write_Value),
    .Value(Value));
  Multiplexer #(.select(2), .width(32), .enable("false")) multiplexer_1 (
    .in0(B1), .in1(B2), .in2(B3), .in3(B4), .out(multiplexer_1_out), .sel(priority_encoder_1_out));
  Priority_Encoder #(.select(2)) priority_encoder_1 (
    .in0(V1), .in1(V2), .in2(V3), .in3(V4), .out(priority_encoder_1_out), .en_in(1'b1));  // open: gs, en_out
  // Probe on priority_encoder_1_out
  and and_2 (and_2_out, ~V4, ~V3, ~V2, ~V1);  // AND_Gate
  Register #(.width(32), .trigger("high")) register_6 (
    .D(multiplexer_1_out), .en(not_2_out), .Q(DataOut), .clk(in_7));  // open: clr
  not not_2 (not_2_out, and_2_out);
  and and_3 (out_17, Read, and_2_out);

  // Other names for the same wires on the sheet: CLK = in_7; CLR = in_8; Data_Output[31:0] = DataOut; Miss = out_17;
  //   RAM_DIR[5:2] = {index, offset}; tag[11:0] = RAM_DIR[17:6]
endmodule

module line (
  input  [11:0] Tag,
  input  Write_Value,
  input  [1:0] offset,
  input  Write,
  input  clock,
  input  Read,
  input  reset,
  input  ACt,
  input  [31:0] in_9,
  input  [31:0] in_10,
  input  [31:0] in_11,
  input  [31:0] in_12,
  input  [31:0] Value,
  output [31:0] out_14,
  output out_15
);

  wire comparator_1_eq, L1, L2, L3, L4, or_1_out, or_2_out, or_3_out, or_4_out, or_5_out, or_6_out, TAG_2_q,
       Valido_q, write_t;
  wire [11:0] TAG_q;
  wire [31:0] _1, _2, _3, _4, D_1, D_2, D_3, D_4;

  Demultiplexer #(.select(2), .enable("false")) demultiplexer_1 (
    .out0(L1), .out1(L2), .out2(L3), .out3(L4), .in(Write_Value), .sel(offset));
  or or_1 (or_1_out, L1, write_t);
  Register #(.width(12)) u_TAG (.D(Tag), .en(Write), .Q(TAG_q), .clk(clock), .clr(reset));
  Register #(.width(32), .trigger("high")) register_1 (.D(D_1), .en(or_1_out), .Q(_1), .clk(clock), .clr(reset));
  Register #(.width(1)) TAG_2 (.D(Write), .Q(TAG_2_q), .clk(clock));  // open: en, clr
  Comparator #(.width(12)) comparator_1 (.a(Tag), .b(TAG_q), .eq(comparator_1_eq));  // open: gt, lt
  or or_2 (or_2_out, L2, write_t);
  or or_3 (or_3_out, Write, TAG_2_q);
  and and_1 (out_15, Read, comparator_1_eq, Valido_q, ACt);
  Register #(.width(32), .trigger("high")) register_2 (.D(D_2), .en(or_2_out), .Q(_2), .clk(clock), .clr(reset));
  and and_2 (write_t, or_3_out, comparator_1_eq);
  Multiplexer #(.width(32), .enable("false")) multiplexer_1 (.in0(in_9), .in1(Value), .out(D_1), .sel(Write_Value));
  Multiplexer #(.width(32), .enable("false")) multiplexer_2 (.in0(in_12), .in1(Value), .out(D_4), .sel(Write_Value));
  or or_4 (or_4_out, Valido_q, write_t);
  Register #(.width(32), .trigger("high")) register_3 (.D(D_3), .en(or_5_out), .Q(_3), .clk(clock), .clr(reset));
  or or_5 (or_5_out, L3, write_t);
  Multiplexer #(.width(32), .enable("false")) multiplexer_3 (.in0(in_10), .in1(Value), .out(D_2), .sel(Write_Value));
  Multiplexer #(.select(2), .width(32), .enable("false")) multiplexer_4 (
    .in0(_1), .in1(_2), .in2(_3), .in3(_4), .out(out_14), .sel(offset));
  D_Flip_Flop #(.trigger("high")) Valido (
    .clk(clock), .D(or_4_out), .Q(Valido_q), .reset(reset));  // open: Qn, preset, en
  Multiplexer #(.width(32), .enable("false")) multiplexer_5 (.in0(in_11), .in1(Value), .out(D_3), .sel(Write_Value));
  Register #(.width(32), .trigger("high")) register_4 (.D(D_4), .en(or_6_out), .Q(_4), .clk(clock), .clr(reset));
  or or_6 (or_6_out, L3, write_t);

  // Other names for the same wires on the sheet: CLK = clock; CLR = reset; D1[31:0] = in_9; D2[31:0] = in_10;
  //   D3[31:0] = in_11; D4[31:0] = in_12; DATA[31:0] = out_14; hit = out_15; read_data = Read; write_data = Write
endmodule
